# Fritzing sketch deskinator-wiring (saved by Fritzing 1.0.5)
breadboards: 2

parts:
  IMU = Adafruit BNO085 9-DOF Orientation IMU Fusion [part_number="Addfruit #4754"]
  NEMA17-1 = Stepper Motor - Bipolar
  NEMA17-2 = Stepper Motor - Bipolar
  RBPi = Raspberry Pi 4B
  Edge-Prox-0 = Adafruit APDS9960 Proximity Sensor [part_number="Adafruit #3595"]
  Lipo = 4S Li-ion/LiPo 14.8 V XT60 [package=lipo-2000]
  Vacuum-DC = DC Vacuum Fan 12V
  XL4015-5_1V = DC_DC_XL4015 [package=board_screw]
  Driver-Left = TMC2209 [package=THT]
  Driver-Right = TMC2209 [package=THT]
  EDGE-MUX = Adafruit TCA9548A
  Edge-Prox-1 = Adafruit APDS9960 Proximity Sensor [part_number="Adafruit #3595"]
  Edge-Prox-2 = Adafruit APDS9960 Proximity Sensor [part_number="Adafruit #3595"]
  Wave-Prox-0 = Adafruit APDS9960 Proximity Sensor [part_number="Adafruit #3595"]
  Buzzer = Piezo Speaker
  Edge-Prox-3 = Adafruit APDS9960 Proximity Sensor [part_number="Adafruit #3595"]
  Q1 = MOSFET-NCHANNEL [package=to220v]
  100Ω-Res = 10kΩ Resistor [package="0402 [SMD]"]
  10kΩ-Res = 10kΩ Resistor [package="0402 [SMD]"]
  Q2 = MOSFET-NCHANNEL [package=to220v]
  D1 = Rectifier Diode [part_number=1N4001 package="300 mil [THT]"]

nets:
  GND: IMU.GND, RBPi.GND, Edge-Prox-0.GND, Lipo.-, XL4015-5_1V.IN-, XL4015-5_1V.OUT-, Driver-Left.GND, Driver-Right.GND, EDGE-MUX.GND, Edge-Prox-1.GND, Edge-Prox-2.GND, Wave-Prox-0.GND, Edge-Prox-3.GND, Q1.S, 10kΩ-Res.Pin_1, Q2.S
  VCC: IMU.VCC, RBPi.3V3, Edge-Prox-0.VCC, Driver-Left.VIO, Driver-Right.VIO, EDGE-MUX.VCC, Edge-Prox-1.VCC, Edge-Prox-2.VCC, Wave-Prox-0.VCC, Edge-Prox-3.VCC
  N1: IMU.SCL/SCK/RX, RBPi.GPIO14
  N2: IMU.SDA/MISO/TX, RBPi.GPIO15
  N3: NEMA17-1.A, Driver-Left.M1B
  N4: NEMA17-1.C, Driver-Left.M1A
  N5: NEMA17-1.B, Driver-Left.M2A
  N6: NEMA17-1.D, Driver-Left.M2B
  N7: NEMA17-2.A, Driver-Right.M1B
  N8: NEMA17-2.C, Driver-Right.M1A
  N9: NEMA17-2.B, Driver-Right.M2A
  N10: NEMA17-2.D, Driver-Right.M2B
  N11: RBPi.5V, XL4015-5_1V.OUT+, Buzzer.pin2
  N12: RBPi.GPIO2, EDGE-MUX.INPUTSDA
  N13: RBPi.GPIO3, EDGE-MUX.INPUTSCL
  N14: RBPi.GPIO27, RBPi.GPIO16, Driver-Left.EN, Driver-Right.EN
  N15: RBPi.GPIO22, Driver-Right.Step
  N16: RBPi.GPIO23, Driver-Right.Dir
  N17: RBPi.GPIO5, 100Ω-Res.Pin_0
  N18: RBPi.GPIO12, Q2.G
  N19: RBPi.GPIO20, Driver-Left.Step
  N20: RBPi.GPIO21, Driver-Left.Dir
  N21: Edge-Prox-0.SDA, EDGE-MUX.0SDA
  N22: Edge-Prox-0.SCL, EDGE-MUX.0SCL
  N23: Lipo.+, Vacuum-DC.pin_1, XL4015-5_1V.IN+, Driver-Left.VM, Driver-Right.VM, D1.cathode
  N24: Vacuum-DC.pin_2, Q1.D, D1.anode
  N25: EDGE-MUX.2SDA, Edge-Prox-2.SDA
  N26: EDGE-MUX.2SCL, Edge-Prox-2.SCL
  N27: EDGE-MUX.3SDA, Edge-Prox-3.SDA
  N28: EDGE-MUX.3SCL, Edge-Prox-3.SCL
  N29: EDGE-MUX.4SDA, Wave-Prox-0.SDA
  N30: EDGE-MUX.4SCL, Wave-Prox-0.SCL
  N31: EDGE-MUX.1SDA, Edge-Prox-1.SDA
  N32: EDGE-MUX.1SCL, Edge-Prox-1.SCL
  N33: Buzzer.pin1, Q2.D
  N34: Q1.G, 100Ω-Res.Pin_1, 10kΩ-Res.Pin_0

notes:
  12V
  5.10V

custom parts:
  Adafruit APDS9960 Proximity Sensor: This breakout is chock full o' sensors! Add basic gesture sensing, RGB color sensing, proximity sensing, or ambient light sensing to your project with the Adafruit APDS9960 Proximity, Light, RGB and Gesture Sensor. When connected to your microcontroller (running our library code) it can detect simple gestures (left to right, right to left, up to down, down to up are currently supported),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
  4S Li-ion/LiPo 14.8 V XT60: 4S Li-ion/LiPo pack, 14.8 V nominal (16.8 V full), XT60 connector.
  DC Vacuum Fan 12V: DC Vacuum Fan
  DC_DC_XL4015: DC-DC Converter step down voltage regulator XL4016 custom sketch.
  TMC2209: TMC2209-LA stepper motor controller and driver. Supply voltage 4.75-28V Iphase up to 1.77A rms (2.5A peak)
  Adafruit TCA9548A: You just found the perfect I2C sensor, and you want to wire up two or three or more of them to your Arduino when you realize "Uh oh, this chip has a fixed I2C address, and from what I know about I2C, you cannot have two devices with the same address on the same SDA/SCL pins!" Are you out of luck? You would be, if you didn't have this ultra-cool TCA9548A 1-to-8 I2C multiplexer! Finally, a way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
  10kΩ Resistor: Resistor Basic schematic elements and footprints for 0603, 1206, and PTH resistors.
