# Fritzing sketch deskinator-wiring (saved by Fritzing 1.0.5)
breadboards: 2

parts:
  IMU = Adafruit BNO085 9-DOF Orientation IMU Fusion [part_number="Addfruit #4754"]
  NEMA17-Left = Stepper Motor - Bipolar
  NEMA17-Right = Stepper Motor - Bipolar
  RBPi_4B = Raspberry Pi 4B
  12V-3A-3kmAh = 4S Li-ion/LiPo 14.8 V XT60 [package=lipo-2000]
  Vacuum-DC = DC Vacuum Fan 12V
  Driver-Left = TMC2209 [package=THT]
  Driver-Right = TMC2209 [package=THT]
  LEFT = Adafruit APDS9960 Proximity Sensor [part_number="Adafruit #3595"]
  RIGHT = Adafruit APDS9960 Proximity Sensor [part_number="Adafruit #3595"]
  GESTURE = Adafruit APDS9960 Proximity Sensor [part_number="Adafruit #3595"]
  MOSFET = MOSFET-NCHANNEL [package=to220v]
  100Ω-Res = 10kΩ Resistor [package="0402 [SMD]"]
  10kΩ-Res = 10kΩ Resistor [package="0402 [SMD]"]
  DIODE = Rectifier Diode [part_number=1N4001 package="300 mil [THT]"]
  LED1 = smd LED [color="Red (633nm)" package="1206 [SMD]"]
  5V-2_4A-3kmAh = LIPO-2000mAh [package=lipo-2000]
  Resistor = Resistor [tolerance=±5% power=0.25W resistance=220 package=THT]

nets:
  N1: IMU.SCL/SCK/RX, RBPi_4B.GPIO13
  N2: IMU.SDA/MISO/TX, RBPi_4B.GPIO6
  N3: NEMA17-Left.A, Driver-Left.M1B
  N4: NEMA17-Left.C, Driver-Left.M1A
  N5: NEMA17-Left.B, Driver-Left.M2A
  N6: NEMA17-Left.D, Driver-Left.M2B
  N7: NEMA17-Right.A, Driver-Right.M1B
  N8: NEMA17-Right.C, Driver-Right.M1A
  N9: NEMA17-Right.B, Driver-Right.M2A
  N10: NEMA17-Right.D, Driver-Right.M2B
  VCC: RBPi_4B.3V3, LEFT.VCC, RIGHT.VCC, GESTURE.VCC
  N11: RBPi_4B.5V, 5V-2_4A-3kmAh.+
  N12: RBPi_4B.GPIO2, GESTURE.SDA
  N13: RBPi_4B.GPIO3, GESTURE.SCL
  GND: RBPi_4B.GND, 12V-3A-3kmAh.-, Driver-Left.GND, Driver-Right.GND, LEFT.GND, RIGHT.GND, GESTURE.GND, MOSFET.S, 10kΩ-Res.Pin_1, LED1.anode, 5V-2_4A-3kmAh.-
  N14: RBPi_4B.GPIO27, Driver-Right.EN
  N15: RBPi_4B.GPIO22, Driver-Right.Step
  N16: RBPi_4B.GPIO23, Driver-Right.Dir
  N17: RBPi_4B.GPIO24, RIGHT.SCL
  N18: RBPi_4B.GPIO25, RIGHT.SDA
  N19: RBPi_4B.GPIO5, 100Ω-Res.Pin_0
  N20: RBPi_4B.GPIO12, Resistor.Pin_1
  N21: RBPi_4B.GPIO19, LEFT.SDA
  N22: RBPi_4B.GPIO16, Driver-Left.EN
  N23: RBPi_4B.GPIO26, LEFT.SCL
  N24: RBPi_4B.GPIO20, Driver-Left.Step
  N25: RBPi_4B.GPIO21, Driver-Left.Dir
  N26: 12V-3A-3kmAh.+, Vacuum-DC.pin_1, Driver-Left.VM, Driver-Right.VM, DIODE.cathode
  N27: Vacuum-DC.pin_2, MOSFET.D, DIODE.anode
  N28: MOSFET.G, 100Ω-Res.Pin_1, 10kΩ-Res.Pin_0
  N29: LED1.cathode, Resistor.Pin_0

notes:
  12V
  5.10V
  3V

custom parts:
  4S Li-ion/LiPo 14.8 V XT60: 4S Li-ion/LiPo pack, 14.8 V nominal (16.8 V full), XT60 connector.
  DC Vacuum Fan 12V: DC Vacuum Fan
  TMC2209: TMC2209-LA stepper motor controller and driver. Supply voltage 4.75-28V Iphase up to 1.77A rms (2.5A peak)
  Adafruit APDS9960 Proximity Sensor: This breakout is chock full o' sensors! Add basic gesture sensing, RGB color sensing, proximity sensing, or ambient light sensing to your project with the Adafruit APDS9960 Proximity, Light, RGB and Gesture Sensor. When connected to your microcontroller (running our library code) it can detect simple gestures (left to right, right to left, up to down, down to up are currently supported),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
  10kΩ Resistor: Resistor Basic schematic elements and footprints for 0603, 1206, and PTH resistors.
